# Fritzing sketch segBot (saved by Fritzing 0.9.0b)
breadboards: 1

parts:
  U1 = L298 [package=multiwatt15]
  U2 = L298 [package=multiwatt15]
  RIGHT_WHEEL = DC Motor
  LEFT_WHEEL = DC Motor
  Atmega1 = ATmega644 [package=pdpi]
  Part1 = Triple Axis Accelerometer Breakout - ADXL345
  D1 = Rectifier Diode [part_number=1N4001 package="300 mil [THT]"]
  D2 = Rectifier Diode [part_number=1N4001 package="300 mil [THT]"]
  D4 = Rectifier Diode [part_number=1N4001 package="300 mil [THT]"]
  D5 = Rectifier Diode [part_number=1N4001 package="300 mil [THT]"]
  D6 = Rectifier Diode [part_number=1N4001 package="300 mil [THT]"]
  D7 = Rectifier Diode [part_number=1N4001 package="300 mil [THT]"]
  D8 = Rectifier Diode [part_number=1N4001 package="300 mil [THT]"]
  C1 = Ceramic Capacitor [capacitance=100nF package="100 mil [THT, multilayer]"]
  C2 = Ceramic Capacitor [capacitance=100nF package="100 mil [THT, multilayer]"]
  D3 = Rectifier Diode [part_number=1N4001 package="300 mil [THT]"]
  C5 = Ceramic Capacitor [capacitance=100nF package="100 mil [THT, multilayer]"]
  C6 = Ceramic Capacitor [capacitance=100nF package="100 mil [THT, multilayer]"]
  XTAL1 = Crystal [frequency="16 Mhz" package=SMD]
  C8 = Ceramic Capacitor [capacitance="100 nF" package="0603 [SMD, multilayer]"]
  C7 = Ceramic Capacitor [capacitance=1pF package="200 mil [THT, multilayer]"]
  J1 = AVR ISP 6 Pin [package=2x3-ns]
  U5 = 2.4GHz Low Power Transceiver [package=qfn20]
  S1 = Pushbutton [package=THT]
  R5 = Resistor [tolerance=±5% resistance=10k package=THT]
  Atmega3 = ATmega644 [package=pdpi]
  Part2 = Triple Axis Accelerometer Breakout - ADXL345
  XTAL2 = Crystal [frequency="16 Mhz" package=SMD]
  C9 = Ceramic Capacitor [capacitance=1pF package="200 mil [THT, multilayer]"]
  C10 = Ceramic Capacitor [capacitance="100 nF" package="0603 [SMD, multilayer]"]
  J2 = AVR ISP 6 Pin [package=2x3-ns]
  U6 = 2.4GHz Low Power Transceiver [package=qfn20]
  S2 = Pushbutton [package=THT]
  R6 = Resistor [tolerance=±5% resistance=10k package=THT]

nets:
  GND: U1.CSA, U1.GND, U1.CSB, U2.CSA, U2.GND, U2.CSB, Atmega1.GND, Part1.GND, D4.anode, D7.anode, D8.anode, C1.0, C2.0, D3.anode, C5.0, C6.0, C8.0, C7.0, J1.6, U5.VSS, S1.leg1, Atmega3.GND, Part2.GND, C9.0, C10.0, J2.6, U6.VSS, S2.leg1
  N1: U1.OUT1, U2.OUT1, LEFT_WHEEL.pin_1, D1.anode, D3.cathode
  N2: U1.OUT2, U2.OUT2, LEFT_WHEEL.pin_2, D2.anode, D4.cathode
  5V: U1.VS, U2.VS, Atmega1.VCC, Atmega1.AVCC, Part1.VCC, C1.1, C6.1, J1.2, R5.Pin_1, Atmega3.VCC, Atmega3.AVCC, Part2.VCC, J2.2, R6.Pin_1
  N3: U1.IN1, U2.IN1, Atmega1.PD2
  N4: U1.ENA, U2.ENA, Atmega1.PB3
  N5: U1.IN2, U2.IN2, Atmega1.PD3
  12V: U1.VLS, U2.VLS, D1.cathode, D2.cathode, D5.cathode, D6.cathode, C2.1, C5.1
  N6: U1.IN3, U2.IN3, Atmega1.PD4
  N7: U1.ENB, U2.ENB, Atmega1.PB4
  N8: U1.IN4, U2.IN4, Atmega1.PD5
  N9: U1.OUT3, U2.OUT3, RIGHT_WHEEL.pin_1, D6.anode, D8.cathode
  N10: U1.OUT4, U2.OUT4, RIGHT_WHEEL.pin_2, D5.anode, D7.cathode
  N11: Atmega1.PB5, J1.1, U5.MISO
  N12: Atmega1.PB6, J1.4, U5.MOSI
  N13: Atmega1.PB7, J1.3, U5.SCK
  N14: Atmega1.RESET, J1.5, S1.leg0, R5.Pin_0
  N15: Atmega1.XTAL2, XTAL1.pin_0, C7.1
  N16: Atmega1.XTAL1, XTAL1.pin_1, C8.1
  N17: Atmega1.PD6, U5.CSN
  N18: Atmega1.PD7, U5.CE
  N19: Atmega1.PC0, Part1.SCL
  N20: Atmega1.PC1, Part1.SDA
  NC: Part1.CS, Part1.INT1, Part1.INT2, Part1.SDO, U5.IRQ, U5.XC2, U5.XC1, U5.VDD_PA, U5.ANT1, U5.ANT2, U5.IREF, U5.DVDD, Part2.CS, Part2.INT1, Part2.INT2, Part2.SDO, U6.IRQ, U6.XC2, U6.XC1, U6.VDD_PA, U6.ANT1, U6.ANT2, U6.IREF, U6.DVDD
  3.6V: U5.VDD, U6.VDD
  N21: Atmega3.PB5, J2.1, U6.MISO
  N22: Atmega3.PB6, J2.4, U6.MOSI
  N23: Atmega3.PB7, J2.3, U6.SCK
  N24: Atmega3.RESET, J2.5, S2.leg0, R6.Pin_0
  N25: Atmega3.XTAL2, XTAL2.pin_0, C9.1
  N26: Atmega3.XTAL1, XTAL2.pin_1, C10.1
  N27: Atmega3.PD6, U6.CSN
  N28: Atmega3.PD7, U6.CE
  N29: Atmega3.PC0, Part2.SCL
  N30: Atmega3.PC1, Part2.SDA
